// Logisim project sampler.circ as structural Verilog: 2 circuits, main circuit main
module main (
);

  wire button_1_out, clock_1_out, d_ff_1_q, d_ff_2_q, d_ff_2_qn, d_ff_3_q;
  wire [7:0] playback_1_data;

  Clock clock_1 (.out(clock_1_out));
  Button button_1 (.out(button_1_out));
  D_Flip_Flop d_ff_1 (.clk(button_1_out), .D(1'b1), .Q(d_ff_1_q), .reset(d_ff_3_q));  // open: Qn, preset, en
  D_Flip_Flop d_ff_2 (
    .clk(clock_1_out), .D(d_ff_1_q), .Q(d_ff_2_q), .Qn(d_ff_2_qn), .reset(d_ff_3_q));  // open: preset, en
  playback playback_1 (.DATA(playback_1_data), .CLK(clock_1_out), .RESET(d_ff_2_q), .PLAY(d_ff_2_qn));
  D_Flip_Flop d_ff_3 (.clk(clock_1_out), .D(d_ff_2_q), .Q(d_ff_3_q), .reset(d_ff_3_q));  // open: Qn, preset, en
  DotMatrix #(.matrixcols(8), .matrixrows(1), .dotshape("circle")) dotmatrix_1 (
    .col0(playback_1_data[7]), .col1(playback_1_data[6]), .col2(playback_1_data[5]),
    .col3(playback_1_data[4]), .col4(playback_1_data[3]), .col5(playback_1_data[2]),
    .col6(playback_1_data[1]), .col7(playback_1_data[0]));

  // Notes on the sheet:
  //   Playback
endmodule

module playback (
  input  PLAY,
  input  RESET,
  input  CLK,
  output [7:0] DATA
);

  wire and_1_out, counter_1_carry;
  wire [7:0] counter_1_q;

  Counter counter_1 (
    .count(and_1_out), .Q(counter_1_q), .carry(counter_1_carry), .clk(CLK), .clr(RESET));  // open: load, D
  and and_1 (and_1_out, ~counter_1_carry, PLAY);  // AND_Gate
  ROM rom_1 (.addr(counter_1_q), .data(DATA));  // open: sel

  // Notes on the sheet:
  //   ROM
  //   contents of rom_1 (hex, n*v repeats v):
  //   0 1 2 3 4 5 6 7 8 9 a b c d e f 10 11 12 13 14 15 16 17 18 19 1a 1b 1c 1d 1e 1f 20 21 22 23 24 25 26
  //   27 28 29 2a 2b 2c 2d 2e 2f 30 31 32 33 34 35 36 37 38 39 3a 3b 3c 3d 3e 3f 40 41 42 43 44 45 46 47
  //   48 49 4a 4b 4c 4d 4e 4f 50 51 52 53 54 55 56 57 58 59 5a 5b 5c 5d 5e 5f 60 61 62 63 64 65 66 67 68
  //   69 6a 6b 6c 6d 6e 6f 70 71 72 73 74 75 76 77 78 79 7a 7b 7c 7d 7e 7f 80 81 82 83 84 85 86 87 88 89
  //   8a 8b 8c 8d 8e 8f 90 91 92 93 94 95 96 97 98 99 9a 9b 9c 9d 9e 9f a0 a1 a2 a3 a4 a5 a6 a7 a8 a9 aa
  //   ab ac ad ae af b0 b1 b2 b3 b4 b5 b6 b7 b8 b9 ba bb bc bd be bf c0 c1 c2 c3 c4 c5 c6 c7 c8 c9 ca cb
  //   cc cd ce cf d0 d1 d2 d3 d4 d5 d6 d7 d8 d9 da db dc dd de df e0 e1 e2 e3 e4 e5 e6 e7 e8 e9 ea eb ec
  //   ed ee ef f0 f1 f2 f3 f4 f5 f6 f7 f8 f9 fa fb fc fd fe ff
endmodule
